// Logisim project Ep01.circ as structural Verilog: 5 circuits, main circuit Parte 2
module meio_somador (
  input  A0,
  input  B0,
  output SOMA,
  output Cout
);

  xor xor_1 (SOMA, A0, B0);
  and and_1 (Cout, A0, B0);

  // Notes on the sheet:
  //   Se temos 1 e 1 ele pega e faz carry out e guarda o +1
endmodule

module Somador_4_bits (
  input  A0,
  input  A1,
  input  A2,
  input  A3,
  input  B0,
  input  B1,
  input  B2,
  input  B3,
  input  Ci0,
  output S0,
  output S1,
  output S2,
  output S3,
  output Co,
  output Overflow
);

  wire somador_completo_1_co, somador_completo_2_co, somador_completo_3_co;

  somador_completo somador_completo_1 (.A(A0), .B(B0), .Ci(Ci0), .S(S0), .Co(somador_completo_1_co));
  somador_completo somador_completo_2 (.A(A1), .B(B1), .Ci(somador_completo_1_co), .S(S1), .Co(somador_completo_2_co));
  somador_completo somador_completo_3 (.A(A2), .B(B2), .Ci(somador_completo_2_co), .S(S2), .Co(somador_completo_3_co));
  somador_completo somador_completo_4 (.A(A3), .B(B3), .Ci(somador_completo_3_co), .S(S3), .Co(Co));
  // Probe on somador_completo_1_co
  // Probe on somador_completo_2_co
  // Probe on somador_completo_3_co
  xor xor_1 (Overflow, somador_completo_3_co, Co);

  // Notes on the sheet:
  //   Ci1 = Co0     Ci2 = Co1     Ci3 = Co2
  //   Overflow = Co3 XOR Co2
endmodule

module somador_completo (
  input  A,
  input  B,
  input  Ci,
  output S,
  output Co
);

  wire meio_somador_1_cout, meio_somador_1_soma, meio_somador_2_cout;

  meio_somador meio_somador_1 (.A0(A), .B0(B), .SOMA(meio_somador_1_soma), .Cout(meio_somador_1_cout));
  meio_somador meio_somador_2 (.A0(meio_somador_1_soma), .B0(Ci), .SOMA(S), .Cout(meio_somador_2_cout));
  or or_1 (Co, meio_somador_1_cout, meio_somador_2_cout);
endmodule

module Parte_2 (
  input  A0,
  input  A1,
  input  A2,
  input  A3,
  input  B0,
  input  B1,
  input  B2,
  input  B3,
  input  Ci0,
  output S0,
  output S1,
  output S2,
  output S3,
  output Co,
  output Overflow
);

  wire decodificador_1_a, decodificador_1_b, decodificador_1_c, decodificador_1_d, decodificador_1_e,
       decodificador_1_f, decodificador_1_g, decodificador_2_a, decodificador_2_b, decodificador_2_c,
       decodificador_2_d, decodificador_2_e, decodificador_2_f, decodificador_2_g, decodificador_3_a,
       decodificador_3_b, decodificador_3_c, decodificador_3_d, decodificador_3_e, decodificador_3_f,
       decodificador_3_g;

  Somador_4_bits somador_4_bits_1 (
    .A0(A0), .A1(A1), .A2(A2), .A3(A3), .B0(B0), .B1(B1), .B2(B2), .B3(B3), .Ci0(Ci0), .S0(S0), .S1(S1),
    .S2(S2), .S3(S3), .Co(Co), .Overflow(Overflow));
  decodificador decodificador_1 (
    .input0(A3), .input1(A2), .input2(A1), .input3(A0), .a(decodificador_1_a), .b(decodificador_1_b),
    .c(decodificador_1_c), .d(decodificador_1_d), .e(decodificador_1_e), .f(decodificador_1_f),
    .g(decodificador_1_g));
  decodificador decodificador_2 (
    .input0(S3), .input1(S2), .input2(S1), .input3(S0), .a(decodificador_2_a), .b(decodificador_2_b),
    .c(decodificador_2_c), .d(decodificador_2_d), .e(decodificador_2_e), .f(decodificador_2_f),
    .g(decodificador_2_g));
  decodificador decodificador_3 (
    .input0(B3), .input1(B2), .input2(B1), .input3(B0), .a(decodificador_3_a), .b(decodificador_3_b),
    .c(decodificador_3_c), .d(decodificador_3_d), .e(decodificador_3_e), .f(decodificador_3_f),
    .g(decodificador_3_g));
  _7_Segment_Display u_7_segment_display_1 (
    .g(decodificador_1_g), .f(decodificador_1_f), .a(decodificador_1_a), .b(decodificador_1_b),
    .e(decodificador_1_e), .d(decodificador_1_d), .c(decodificador_1_c));  // open: dp
  _7_Segment_Display u_7_segment_display_2 (
    .g(decodificador_2_g), .f(decodificador_2_f), .a(decodificador_2_a), .b(decodificador_2_b),
    .e(decodificador_2_e), .d(decodificador_2_d), .c(decodificador_2_c));  // open: dp
  _7_Segment_Display u_7_segment_display_3 (
    .g(decodificador_3_g), .f(decodificador_3_f), .a(decodificador_3_a), .b(decodificador_3_b),
    .e(decodificador_3_e), .d(decodificador_3_d), .c(decodificador_3_c));  // open: dp

  // Notes on the sheet:
  //   Somador 4 bits
  //   Decodificador A
  //   Decodificador SOMA
  //   Decodificador B
endmodule

module decodificador (
  input  input0,
  input  input1,
  input  input2,
  input  input3,
  output a,
  output b,
  output c,
  output d,
  output e,
  output f,
  output g
);

  wire and_1_out, and_2_out, and_3_out, and_4_out, and_5_out, and_6_out, and_7_out, and_8_out, and_9_out,
       and_10_out, and_11_out, and_12_out, and_13_out, and_14_out, and_15_out, and_16_out, and_17_out,
       and_18_out, and_19_out, and_20_out, and_21_out, and_22_out, and_23_out, and_24_out, and_25_out,
       and_26_out, and_27_out, and_28_out, and_29_out, and_30_out, and_31_out, and_32_out, and_33_out,
       and_34_out, and_35_out, not_1_out, not_2_out, not_3_out, not_4_out, not_5_out, not_6_out, not_7_out,
       not_8_out, not_9_out, not_10_out, not_11_out, not_12_out, not_13_out, not_14_out, not_15_out,
       not_16_out, not_17_out, not_18_out, not_19_out, not_20_out, not_21_out, not_22_out, not_24_out,
       not_25_out, not_26_out, not_27_out, not_28_out, not_29_out, not_30_out, not_31_out, not_32_out,
       not_33_out, not_34_out, not_35_out, not_36_out, not_37_out, not_38_out, not_39_out, not_40_out,
       not_41_out, not_42_out, not_43_out, not_44_out;

  not not_1 (not_1_out, input1);
  and and_1 (and_1_out, not_1_out, not_2_out);
  not not_2 (not_2_out, input3);
  not not_3 (not_3_out, input0);
  and and_2 (and_2_out, not_3_out, input2);
  not not_4 (not_4_out, input0);
  and and_3 (and_3_out, not_4_out, input1, input3);
  and and_4 (and_4_out, input1, input2);
  and and_5 (and_5_out, input0, not_5_out, not_6_out);
  not not_5 (not_5_out, input1);
  not not_6 (not_6_out, input2);
  and and_6 (and_6_out, input0, not_7_out);
  not not_7 (not_7_out, input3);
  not not_8 (not_8_out, input0);
  and and_7 (and_7_out, not_8_out, not_9_out);
  not not_9 (not_9_out, input1);
  not not_10 (not_10_out, input0);
  and and_8 (and_8_out, not_10_out, not_11_out, not_12_out);
  not not_11 (not_11_out, input2);
  not not_12 (not_12_out, input3);
  not not_13 (not_13_out, input1);
  and and_9 (and_9_out, not_13_out, not_14_out);
  not not_14 (not_14_out, input3);
  not not_15 (not_15_out, input0);
  and and_10 (and_10_out, not_15_out, input2, input3);
  and and_11 (and_11_out, input0, not_16_out, input3);
  not not_16 (not_16_out, input2);
  not not_17 (not_17_out, input0);
  and and_12 (and_12_out, not_17_out, not_18_out);
  not not_18 (not_18_out, input2);
  not not_19 (not_19_out, input0);
  and and_13 (and_13_out, not_19_out, input3);
  not not_20 (not_20_out, input2);
  and and_14 (and_14_out, not_20_out, input3);
  not not_21 (not_21_out, input0);
  and and_15 (and_15_out, not_21_out, input1);
  and and_16 (and_16_out, input0, not_22_out);
  not not_22 (not_22_out, input1);
  // NOT_Gate not_23 has open pins: in=input3, out=open
  not not_24 (not_24_out, input0);
  and and_17 (and_17_out, not_24_out, not_25_out, not_26_out);
  not not_25 (not_25_out, input1);
  not not_26 (not_26_out, input3);
  not not_27 (not_27_out, input1);
  and and_18 (and_18_out, not_27_out, input2, input3);
  and and_19 (and_19_out, input1, not_28_out, input3);
  not not_28 (not_28_out, input2);
  and and_20 (and_20_out, input1, input2, not_29_out);
  not not_29 (not_29_out, input3);
  and and_21 (and_21_out, input0, not_30_out);
  not not_30 (not_30_out, input2);
  not not_31 (not_31_out, input1);
  and and_22 (and_22_out, not_31_out, not_32_out);
  not not_32 (not_32_out, input3);
  and and_23 (and_23_out, input2, not_33_out);
  not not_33 (not_33_out, input3);
  and and_24 (and_24_out, input0, input2);
  and and_25 (and_25_out, input0, input1);
  not not_34 (not_34_out, input2);
  and and_26 (and_26_out, not_34_out, not_35_out);
  not not_35 (not_35_out, input3);
  not not_36 (not_36_out, input0);
  and and_27 (and_27_out, not_36_out, input1, not_37_out);
  not not_37 (not_37_out, input2);
  and and_28 (and_28_out, input1, not_38_out);
  not not_38 (not_38_out, input3);
  and and_29 (and_29_out, input0, not_39_out);
  not not_39 (not_39_out, input1);
  and and_30 (and_30_out, input0, input2);
  not not_40 (not_40_out, input1);
  and and_31 (and_31_out, not_40_out, input2);
  and and_32 (and_32_out, input2, not_41_out);
  not not_41 (not_41_out, input3);
  not not_42 (not_42_out, input0);
  and and_33 (and_33_out, not_42_out, input1, not_43_out);
  not not_43 (not_43_out, input2);
  and and_34 (and_34_out, input0, not_44_out);
  not not_44 (not_44_out, input1);
  and and_35 (and_35_out, input0, input3);
  or or_1 (b, and_7_out, and_8_out, and_9_out, and_10_out, and_11_out);
  or or_2 (d, and_17_out, and_18_out, and_19_out, and_20_out, and_21_out);
  or or_3 (e, and_22_out, and_23_out, and_24_out, and_25_out);
  or or_4 (f, and_26_out, and_27_out, and_28_out, and_29_out, and_30_out);
  or or_5 (g, and_31_out, and_32_out, and_33_out, and_34_out, and_35_out);
  or or_6 (a, and_1_out, and_2_out, and_3_out, and_4_out, and_5_out, and_6_out);
  or or_7 (c, and_12_out, and_13_out, and_14_out, and_15_out, and_16_out, and_16_out);
endmodule
