// Logisim project ep02.circ as structural Verilog: 6 circuits, main circuit meio somador
module meio_somador (
  input  in_1,
  input  in_2,
  output SOMA,
  output carry_out
);

  xor xor_1 (SOMA, in_1, in_2);
  and and_1 (carry_out, in_1, in_2);

  // Notes on the sheet:
  //   Se temos 1 e 1 ele pega e faz carry out e guarda o +1
endmodule

module Somador_4_bits (
  input  a0,
  input  a1,
  input  a2,
  input  a3,
  input  in_5,
  input  in_6,
  input  in_7,
  input  in_8,
  output out_9,
  output out_10,
  output out_11,
  output out_12,
  output out_13
);

  wire main_1_out_5, main_2_out_5, main_3_out_5;

  Main main_1 (.in_1(a0), .in_2(in_5), .in_3(1'b0), .Soma_Final(out_9), .out_5(main_1_out_5));
  Main main_2 (.in_1(a1), .in_2(in_6), .in_3(main_1_out_5), .Soma_Final(out_10), .out_5(main_2_out_5));
  Main main_3 (.in_1(a2), .in_2(in_7), .in_3(main_2_out_5), .Soma_Final(out_11), .out_5(main_3_out_5));
  Main main_4 (.in_1(a3), .in_2(in_8), .in_3(main_3_out_5), .Soma_Final(out_12), .out_5(out_13));
endmodule

module Main (
  input  in_1,
  input  in_2,
  input  in_3,
  output Soma_Final,
  output out_5
);

  wire meio_somador_1_carry_out, meio_somador_1_soma, meio_somador_2_carry_out;

  meio_somador meio_somador_1 (
    .in_1(in_2), .in_2(in_3), .SOMA(meio_somador_1_soma), .carry_out(meio_somador_1_carry_out));
  meio_somador meio_somador_2 (
    .in_1(meio_somador_1_soma), .in_2(in_1), .SOMA(Soma_Final), .carry_out(meio_somador_2_carry_out));
  or or_1 (out_5, meio_somador_1_carry_out, meio_somador_2_carry_out);
endmodule

module Parte_2 (
  input  A0,
  input  A1,
  input  A2,
  input  A3,
  input  B0,
  input  B1,
  input  B2,
  input  B3,
  output out_9
);

  wire somador_4_bits_1_out_9, somador_4_bits_1_out_10, somador_4_bits_1_out_11, somador_4_bits_1_out_12;

  decodificador decodificador_1 (.input0(A0), .input1(A1), .input2(A2), .input3(A3));  // open: a, b, c, d, e, f, g
  Somador_4_bits somador_4_bits_1 (
    .a0(A0), .a1(A1), .a2(A2), .a3(A3), .in_5(B0), .in_6(B1), .in_7(B2), .in_8(B2),
    .out_9(somador_4_bits_1_out_9), .out_10(somador_4_bits_1_out_10), .out_11(somador_4_bits_1_out_11),
    .out_12(somador_4_bits_1_out_12), .out_13(out_9));
  // Probe on out_9
  decodificador decodificador_2 (.input0(B2), .input1(B2), .input2(B1), .input3(B0));  // open: a, b, c, d, e, f, g
  decodificador decodificador_3 (
    .input0(somador_4_bits_1_out_9), .input1(somador_4_bits_1_out_10), .input2(somador_4_bits_1_out_11),
    .input3(somador_4_bits_1_out_12));  // open: a, b, c, d, e, f, g

  assign B3 = B2;
endmodule

module decodificador (
  input  input0,
  input  input1,
  input  input2,
  input  input3,
  output a,
  output b,
  output c,
  output d,
  output e,
  output f,
  output g
);

  wire and_1_out, and_2_out, and_3_out, and_4_out, and_5_out, and_6_out, and_7_out, and_8_out, and_9_out,
       and_10_out, and_11_out, and_12_out, and_13_out, and_14_out, and_15_out, and_16_out, and_17_out,
       and_18_out, and_19_out, and_20_out, and_21_out, and_22_out, and_23_out, and_24_out, and_25_out,
       and_26_out, and_27_out, and_28_out, and_29_out, and_30_out, and_31_out, and_32_out, and_33_out,
       and_34_out, and_35_out, and_36_out, not_1_out, not_2_out, not_3_out, not_4_out, not_5_out, not_6_out,
       not_7_out, not_8_out, not_9_out, not_10_out, not_11_out, not_12_out, not_13_out, not_14_out,
       not_15_out, not_16_out, not_17_out, not_18_out, not_19_out, not_20_out, not_21_out, not_22_out,
       not_23_out, not_24_out, not_25_out, not_26_out, not_27_out, not_28_out, not_29_out, not_30_out,
       not_31_out, not_32_out, not_33_out, not_34_out, not_35_out, not_36_out, not_37_out, not_38_out,
       not_39_out, not_40_out, not_41_out, not_42_out, not_43_out, not_44_out;

  not not_1 (not_1_out, input1);
  and and_1 (and_1_out, not_1_out, not_2_out);
  not not_2 (not_2_out, input3);
  not not_3 (not_3_out, input0);
  and and_2 (and_2_out, not_3_out, input2);
  not not_4 (not_4_out, input0);
  and and_3 (and_3_out, not_4_out, input1, input3);
  and and_4 (and_4_out, input1, input2);
  and and_5 (and_5_out, input0, not_5_out, not_6_out);
  not not_5 (not_5_out, input1);
  not not_6 (not_6_out, input2);
  and and_6 (and_6_out, input0, not_7_out);
  not not_7 (not_7_out, input3);
  not not_8 (not_8_out, input0);
  and and_7 (and_7_out, not_8_out, not_9_out);
  not not_9 (not_9_out, input1);
  not not_10 (not_10_out, input0);
  and and_8 (and_8_out, not_10_out, not_11_out, not_12_out);
  not not_11 (not_11_out, input2);
  not not_12 (not_12_out, input3);
  not not_13 (not_13_out, input1);
  and and_9 (and_9_out, not_13_out, not_14_out);
  not not_14 (not_14_out, input3);
  not not_15 (not_15_out, input0);
  and and_10 (and_10_out, not_15_out, input2, input3);
  and and_11 (and_11_out, input0, not_16_out, input3);
  not not_16 (not_16_out, input2);
  not not_17 (not_17_out, input0);
  and and_12 (and_12_out, not_17_out, not_18_out);
  not not_18 (not_18_out, input2);
  not not_19 (not_19_out, input0);
  and and_13 (and_13_out, not_19_out, input3);
  not not_20 (not_20_out, input2);
  and and_14 (and_14_out, not_20_out, input3);
  not not_21 (not_21_out, input0);
  and and_15 (and_15_out, not_21_out, input1);
  and and_16 (and_16_out, input0, not_22_out);
  not not_22 (not_22_out, input1);
  and and_17 (and_17_out, input0, input2, not_23_out);
  not not_23 (not_23_out, input3);
  not not_24 (not_24_out, input0);
  and and_18 (and_18_out, not_24_out, not_25_out, not_26_out);
  not not_25 (not_25_out, input1);
  not not_26 (not_26_out, input3);
  not not_27 (not_27_out, input1);
  and and_19 (and_19_out, not_27_out, input2, input3);
  and and_20 (and_20_out, input1, not_28_out, input3);
  not not_28 (not_28_out, input2);
  and and_21 (and_21_out, input1, input2, not_29_out);
  not not_29 (not_29_out, input3);
  and and_22 (and_22_out, input0, not_30_out);
  not not_30 (not_30_out, input2);
  not not_31 (not_31_out, input1);
  and and_23 (and_23_out, not_31_out, not_32_out);
  not not_32 (not_32_out, input3);
  and and_24 (and_24_out, input2, not_33_out);
  not not_33 (not_33_out, input3);
  and and_25 (and_25_out, input0, input2);
  and and_26 (and_26_out, input0, input1);
  not not_34 (not_34_out, input2);
  and and_27 (and_27_out, not_34_out, not_35_out);
  not not_35 (not_35_out, input3);
  not not_36 (not_36_out, input0);
  and and_28 (and_28_out, not_36_out, input1, not_37_out);
  not not_37 (not_37_out, input2);
  and and_29 (and_29_out, input1, not_38_out);
  not not_38 (not_38_out, input3);
  and and_30 (and_30_out, input0, not_39_out);
  not not_39 (not_39_out, input1);
  and and_31 (and_31_out, input0, input2);
  not not_40 (not_40_out, input1);
  and and_32 (and_32_out, not_40_out, input2);
  and and_33 (and_33_out, input2, not_41_out);
  not not_41 (not_41_out, input3);
  not not_42 (not_42_out, input0);
  and and_34 (and_34_out, not_42_out, input1, not_43_out);
  not not_43 (not_43_out, input2);
  and and_35 (and_35_out, input0, not_44_out);
  not not_44 (not_44_out, input1);
  and and_36 (and_36_out, input0, input3);
  or or_1 (b, and_7_out, and_8_out, and_9_out, and_10_out, and_11_out);
  or or_2 (d, and_18_out, and_19_out, and_20_out, and_21_out, and_22_out);
  or or_3 (e, and_23_out, and_24_out, and_25_out, and_26_out);
  or or_4 (f, and_27_out, and_28_out, and_29_out, and_30_out, and_31_out);
  or or_5 (g, and_32_out, and_33_out, and_34_out, and_35_out, and_36_out);
  or or_6 (a, and_1_out, and_2_out, and_3_out, and_4_out, and_5_out, and_6_out);
  or or_7 (c, and_12_out, and_13_out, and_14_out, and_15_out, and_16_out, and_17_out);
endmodule

module Ep2 (
  input  a,
  input  b,
  input  [1:0] in_3,
  input  biinvert,
  input  carry_in,
  output out_6,
  output Carry_out
);

  wire and_1_out, main_1_soma_final, multiplexer_1_out, not_1_out, not_2_out, or_1_out;

  Multiplexer multiplexer_1 (.in0(b), .in1(not_1_out), .out(multiplexer_1_out), .sel(biinvert));  // open: en
  not not_1 (not_1_out, b);
  and and_1 (and_1_out, a, multiplexer_1_out);
  or or_1 (or_1_out, a, multiplexer_1_out);
  not not_2 (not_2_out, a);
  Main main_1 (.in_1(a), .in_2(multiplexer_1_out), .in_3(carry_in), .Soma_Final(main_1_soma_final), .out_5(Carry_out));
  Multiplexer #(.select(2)) multiplexer_2 (
    .in0(and_1_out), .in1(or_1_out), .in2(not_2_out), .in3(main_1_soma_final), .out(out_6), .sel(in_3));  // open: en
endmodule
