// Logisim project somador_4_bits.circ as structural Verilog: 3 circuits, main circuit meio somador
module meio_somador (
  input  in_1,
  input  in_2,
  output SOMA,
  output carry_out
);

  xor xor_1 (SOMA, in_1, in_2);
  and and_1 (carry_out, in_1, in_2);

  // Notes on the sheet:
  //   Se temos 1 e 1 ele pega e faz carry out e guarda o +1
endmodule

module Somador_de_4 (
  input  a0,
  input  a1,
  input  a2,
  input  a3,
  input  in_5,
  input  in_6,
  input  in_7,
  input  in_8,
  output out_9,
  output out_10,
  output out_11,
  output out_12,
  output out_13
);

  wire main_1_out_5, main_2_out_5, main_3_out_5;

  Main main_1 (.in_1(a0), .in_2(in_5), .in_3(1'b0), .Soma_Final(out_9), .out_5(main_1_out_5));
  Main main_2 (.in_1(a1), .in_2(in_6), .in_3(main_1_out_5), .Soma_Final(out_10), .out_5(main_2_out_5));
  Main main_3 (.in_1(a2), .in_2(in_7), .in_3(main_2_out_5), .Soma_Final(out_11), .out_5(main_3_out_5));
  Main main_4 (.in_1(a3), .in_2(in_8), .in_3(main_3_out_5), .Soma_Final(out_12), .out_5(out_13));
endmodule

module Main (
  input  in_1,
  input  in_2,
  input  in_3,
  output Soma_Final,
  output out_5
);

  wire meio_somador_1_carry_out, meio_somador_1_soma, meio_somador_2_carry_out;

  meio_somador meio_somador_1 (
    .in_1(in_2), .in_2(in_3), .SOMA(meio_somador_1_soma), .carry_out(meio_somador_1_carry_out));
  meio_somador meio_somador_2 (
    .in_1(meio_somador_1_soma), .in_2(in_1), .SOMA(Soma_Final), .carry_out(meio_somador_2_carry_out));
  or or_1 (out_5, meio_somador_1_carry_out, meio_somador_2_carry_out);
endmodule
